# Fritzing sketch bunkerbox-v3 (saved by Fritzing 0.9.3b)

parts:
  Power_Distribution_Block1 = EPDB104 Power Distribution Block [part_number=EPDB104]
  Power_Distribution_Block2 = EPDB104 Power Distribution Block [part_number=EPDB104]
  Power_Distribution_Block3 = EPDB104 Power Distribution Block [part_number=EPDB104]
  Contactor1 = SC-E2-220VAC Contactor [part_number=SC-E2-220VAC]
  Circuit_Breaker1 = FAZ-BX-2 Circuit Breaker [part_number=FAZ-BX-2]
  Emergency_Stop_Switch = Round Pushbutton
  Power_Indicator = LED - 5mm [color="Red (633nm)" package="5 mm [THT]"]
  Power_Supply1 = NDR-240-24 Power Supply
  Main_Heater_Circuit_Breaker_(40_AMP) = FAZ-BX-2 Circuit Breaker [part_number=FAZ-B40-2]
  Pre_Heater_Circuit_Breaker_(10_AMP) = FAZ-BX-2 Circuit Breaker [part_number=FAZ-B10-2]
  Industrial_Analog_Out_A = TinkerForge Industrial Analog Out Bricklet
  Industrial_Analog_Out_B = TinkerForge Industrial Analog Out Bricklet
  Industrial_Analog_Out_C = TinkerForge Industrial Analog Out Bricklet
  Step-Down_Power_Supply1 = TinkerForge Step-Down Power Supply
  RED1 = TinkerForge RED Brick  # not connected
  Master1 = TinkerForge Master Brick
  Industrial_Quad_Relay1 = TinkerForge Industrial Quad Relay Bricklet
  Master2 = TinkerForge Master Brick
  Barometer1 = TinkerForge Barometer Bricklet
  1Wire1 = Bunker 1Wire Bricklet

nets:
  N1: Power_Distribution_Block1.pin_4, Circuit_Breaker1.2
  N2: Power_Distribution_Block1.pin_5, Contactor1.2_T1
  N3: Power_Distribution_Block2.pin_4, Circuit_Breaker1.4
  N4: Power_Distribution_Block2.pin_5, Contactor1.4_T2
  N5: Power_Distribution_Block3.pin_5, Power_Supply1.GND
  N6: Contactor1.1_L1, Main_Heater_Circuit_Breaker_(40_AMP).2, Pre_Heater_Circuit_Breaker_(10_AMP).2
  N7: Contactor1.3_L2, Main_Heater_Circuit_Breaker_(40_AMP).4, Pre_Heater_Circuit_Breaker_(10_AMP).4
  N8: Contactor1.A1, Emergency_Stop_Switch.leg0, Power_Indicator.cathode
  N9: Contactor1.A2, Circuit_Breaker1.3, Power_Indicator.anode, Power_Supply1.L
  N10: Circuit_Breaker1.1, Emergency_Stop_Switch.leg1, Power_Supply1.N
  N11: Power_Supply1.+V, Step-Down_Power_Supply1.Input_6-27V
  N12: Power_Supply1.-V, Step-Down_Power_Supply1.Input_GND
  N13: Industrial_Analog_Out_A.Bricklet_Connector, Master1.A
  N14: Industrial_Analog_Out_B.Bricklet_Connector, Master1.B
  N15: Industrial_Analog_Out_C.Bricklet_Connector, Master1.C
  N16: Master1.D, Industrial_Quad_Relay1.Bricklet_Connector
  N17: Master2.A, 1Wire1.Bricklet_Connector
  N18: Master2.B, Barometer1.Bricklet_Connector
